# Fritzing sketch RaspedalSketch (saved by Fritzing 0.9.3b)
breadboards: 1

parts:
  Raspberry_Pi_Zero1 = Raspberry Pi Zero
  AMPHENOL_-_ACJS-MHDR_-_JACK_6_35MM1 = AMPHENOL - ACJS-MHDR [package=ACJS-MHDR]  # not connected
  AMPHENOL_-_ACJS-MHDR_-_JACK_6_35MM2 = AMPHENOL - ACJS-MHDR [package=ACJS-MHDR]  # not connected
  S1 = Round Pushbutton
  S2 = Round Pushbutton
  S3 = Round Pushbutton
  S4 = Round Pushbutton
  S5 = Round Pushbutton
  S6 = Round Pushbutton
  LED1 = LED - 5mm [color="Red (633nm)" package="5 mm [THT]"]
  LED2 = LED - 5mm [color="Red (633nm)" package="5 mm [THT]"]
  LED3 = LED - 5mm [color="Red (633nm)" package="5 mm [THT]"]
  LED4 = LED - 5mm [color="Red (633nm)" package="5 mm [THT]"]
  LED5 = LED - 5mm [color="Red (633nm)" package="5 mm [THT]"]
  LED6 = LED - 5mm [color="Red (633nm)" package="5 mm [THT]"]
  U1 = SWITCH_SPDT [package=kps-1290]
  R1 = Rotary Potentiometer (Small) [maximum_resistance=100kΩ package=THT]
  U2 = LM386 [package=dip08]
  R2 = Resistor [tolerance=±5% resistance=4.7k package="2010 [SMD]"]
  R3 = Resistor [tolerance=±5% resistance=300k package="2010 [SMD]"]

nets:
  N1: Raspberry_Pi_Zero1.3v3, U1.O
  N2: Raspberry_Pi_Zero1.GPIO4, R1.wiper
  N3: Raspberry_Pi_Zero1.GPIO27, LED1.anode
  N4: Raspberry_Pi_Zero1.GPIO22, LED2.anode
  N5: Raspberry_Pi_Zero1.GPIO10, U2.OUT
  N6: Raspberry_Pi_Zero1.GPIO9, U2.V+
  N7: Raspberry_Pi_Zero1.GPIO11, U2.BP
  N8: Raspberry_Pi_Zero1.GPIO5, LED3.anode
  N9: Raspberry_Pi_Zero1.GPIO6, LED4.anode
  N10: Raspberry_Pi_Zero1.GPIO13, R3.Pin_1
  N11: Raspberry_Pi_Zero1.GPIO19, LED5.anode
  N12: Raspberry_Pi_Zero1.GPIO26, LED6.anode
  N13: Raspberry_Pi_Zero1.GPIO21, S6.leg1
  N14: Raspberry_Pi_Zero1.GPIO20, S5.leg1
  N15: Raspberry_Pi_Zero1.GPIO16, S4.leg1
  N16: Raspberry_Pi_Zero1.GPIO12, S3.leg1
  N17: Raspberry_Pi_Zero1.GPIO8, U2.GAIN
  N18: Raspberry_Pi_Zero1.GPIO25, S2.leg1
  N19: Raspberry_Pi_Zero1.GPIO24, S1.leg1
  N20: Raspberry_Pi_Zero1.GPIO18, R2.Pin_1
  N21: Raspberry_Pi_Zero1.GND, LED1.cathode, LED2.cathode, LED3.cathode, LED4.cathode, LED5.cathode, LED6.cathode, U1.P, R1.leg1
  N22: Raspberry_Pi_Zero1.5V, S1.leg0, S2.leg0, S3.leg0, S4.leg0, S5.leg0, S6.leg0, R1.leg2

notes:
  Breadboard Notes
  Top: 5V, Gnd
  Bottom: 3.3V, Gnd
  Switch is actually an LED switch, but no part is available.
  See https://www.sparkfun.com/products/11310
  Used for additional volume control
  GPIO18/PWM0 and GPIO13/PWM1 are used for final outputs
  Wire Color Legend
  Red - Power
  Black - Gnd
  Blue - Guitar Ins
  Green - Guitar Out
  Orange - Button/Fx Controls
  Yellow - Fx Lights
  Purple - Routing/Other
  LM386 Chip is actually MCP3202. No fritzing part, but wired correctly
